// Logisim project s-mips.circ as structural Verilog: 23 circuits, main circuit S-MIPS Board
module S_MIPS_Board (
  input  DESHABILITAR_DISPATCHER,
  output halt
);

  wire button_1_out, CLK, CS, d_ff_1_q, LCLR, LoadRAM, LoadRAMOn, LW, R_R_W, R_W, ram_dispatcher_1_finished,
       RCS, Reset_out, RST, TTY_EN;
  wire [2:0] KDB;
  wire [3:0] LMask, Mask, ram_1_read_time, ram_1_write_time, RMask;
  wire [6:0] KDB_DATA, TTY_DATA;
  wire [15:0] Addr, LAddr, RAddr;
  wire [31:0] I0, I1, I2, I3, LData, ram_1_data_out_0, ram_1_data_out_1, ram_1_data_out_2, ram_1_data_out_3,
       RI0, RI1, RI2, RI3;

  TTY #(.rows(25), .cols(80)) tty_1 (.data(TTY_DATA), .clk(CLK), .we(TTY_EN), .clr(RST));
  not not_1 (LoadRAMOn, ram_dispatcher_1_finished);
  RAM_Dispatcher ram_dispatcher_1 (
    .WriteTime(ram_1_write_time), .Clock(CLK), .Data(LData), .Address(LAddr), .Mask(LMask),
    .Finished(ram_dispatcher_1_finished), .Write(LW), .CLR(LCLR));
  Keyboard #(.buflen(64)) keyboard_1 (.clk(CLK), .re(KDB[0]), .avail(KDB[2]), .data(KDB_DATA));  // open: clr
  RAM ram_1 (
    .Address(RAddr), .Data_Out_0(ram_1_data_out_0), .Data_Out_1(ram_1_data_out_1),
    .Data_Out_2(ram_1_data_out_2), .Data_Out_3(ram_1_data_out_3), .Data_In_0(RI0), .Data_In_1(RI1),
    .Data_In_2(RI2), .Data_In_3(RI3), .Mask(RMask), .nRead_Write(R_R_W), .Chip_Select(RCS),
    .Read_Time(ram_1_read_time), .Reset(button_1_out), .Write_Time(ram_1_write_time));
  Button button_1 (.out(button_1_out));
  D_Flip_Flop d_ff_1 (.clk(CLK), .D(1'b1), .Q(d_ff_1_q), .reset(Reset_out));  // open: Qn, preset, en
  Button Reset (.out(Reset_out));
  S_MIPS s_mips_1 (
    .Kbd_Enable(KDB[0]), .Address(Addr), .Kbd_Clear(KDB[1]), .Kbd_Available(KDB[2]), .RAM_In_0(I0),
    .Kbd_ASCII_Data(KDB_DATA), .RAM_In_1(I1), .TTY_Enable(TTY_EN), .RAM_In_2(I2), .RAM_In_3(I3),
    .TTY_ASCII_Data(TTY_DATA), .Reset(RST), .RAM_Out_0(ram_1_data_out_0), .Clock(CLK),
    .RAM_Out_1(ram_1_data_out_1), .Stop(halt), .RAM_Out_2(ram_1_data_out_2), .RAM_Out_3(ram_1_data_out_3),
    .Mask(Mask), .Read_Time(ram_1_read_time), .Write_Time(ram_1_write_time), .nRead_Write(R_W),
    .Chip_Select(CS));
  D_Flip_Flop d_ff_2 (.clk(CLK), .D(d_ff_1_q), .Qn(LCLR), .reset(Reset_out));  // open: Q, preset, en
  or or_1 (RST, LCLR, LoadRAM);
  Clock clock_1 (.out(CLK));
  Multiplexer #(.width(32), .enable("false")) multiplexer_1 (.in0(I0), .in1(LData), .out(RI0), .sel(LoadRAM));
  Multiplexer #(.width(32), .enable("false")) multiplexer_2 (.in0(I1), .in1(LData), .out(RI1), .sel(LoadRAM));
  Multiplexer #(.width(32), .enable("false")) multiplexer_3 (.in0(I2), .in1(LData), .out(RI2), .sel(LoadRAM));
  Multiplexer #(.width(32), .enable("false")) multiplexer_4 (.in0(I3), .in1(LData), .out(RI3), .sel(LoadRAM));
  and and_1 (LoadRAM, ~DESHABILITAR_DISPATCHER, LoadRAMOn);  // AND_Gate
  Multiplexer #(.width(16), .enable("false")) multiplexer_5 (.in0(Addr), .in1(LAddr), .out(RAddr), .sel(LoadRAM));
  Multiplexer #(.width(4), .enable("false")) multiplexer_6 (.in0(Mask), .in1(LMask), .out(RMask), .sel(LoadRAM));
  Multiplexer #(.enable("false")) multiplexer_7 (.in0(CS), .in1(LW), .out(RCS), .sel(LoadRAM));
  Multiplexer #(.enable("false")) multiplexer_8 (.in0(R_W), .in1(LW), .out(R_R_W), .sel(LoadRAM));

  // Notes on the sheet:
  //   NO MODIFICAR
  //   Keyboard
endmodule

module RAM (
  input  [15:0] Address,
  input  [31:0] Data_In_0,
  input  [31:0] Data_In_1,
  input  [31:0] Data_In_2,
  input  [31:0] Data_In_3,
  input  [3:0] Mask,
  input  nRead_Write,
  input  Chip_Select,
  input  Reset,
  output [31:0] Data_Out_0,
  output [31:0] Data_Out_1,
  output [31:0] Data_Out_2,
  output [31:0] Data_Out_3,
  output [3:0] Read_Time,
  output [3:0] Write_Time
);

  wire and_2_out, and_3_out, and_4_out, and_5_out, and_6_out, and_7_out, and_8_out, and_9_out, Changed, CLK,
       comparator_2_eq, comparator_3_eq, comparator_4_eq, comparator_5_eq, comparator_6_eq, Count,
       demultiplexer_3_out0, Idle, Idle_q, Load, Load0, Load1, nand_1_out, or_1_out, or_2_out, or_3_out,
       or_4_out, or_5_out, or_6_out, or_7_out, or_8_out, or_9_out, or_10_out, Proc_q, Update_Mem, Zero_Time;
  wire [3:0] counter_1_q, multiplexer_1_out, subtractor_1_out;
  wire [31:0] register_1_q, register_2_q, register_3_q, register_4_q, register_5_q;

  // Probe on 4'b0011
  // Probe on 4'b0010
  Multiplexer #(.width(4), .enable("false")) multiplexer_1 (
    .in0(4'b0011), .in1(4'b0010), .out(multiplexer_1_out), .sel(nRead_Write));
  or or_1 (or_1_out, Idle, Update_Mem);
  or or_2 (or_2_out, ~Chip_Select, Reset);  // OR_Gate
  Subtractor #(.width(4)) subtractor_1 (.a(multiplexer_1_out), .b(4'b0010), .out(subtractor_1_out));  // open: bin, bout
  D_Flip_Flop u_Idle (.clk(CLK), .D(or_1_out), .Q(Idle_q), .preset(or_2_out));  // open: Qn, en, reset
  Demultiplexer #(.enable("false")) demultiplexer_1 (.out0(Idle), .out1(Load0), .in(Idle_q), .sel(Changed));
  // Probe on counter_1_q
  Counter #(.width(4), .max('hf)) counter_1 (
    .load(Load), .D(subtractor_1_out), .count(Count), .Q(counter_1_q), .clk(CLK), .clr(or_3_out));  // open: carry
  or or_3 (or_3_out, ~Chip_Select, Reset);  // OR_Gate
  Comparator_part #(.width(4), .mode("unsigned")) comparator_1 (
    .a(4'b0000), .b(counter_1_q), .eq(Zero_Time));  // open: gt, lt
  or or_4 (or_4_out, Count, Load0, Load1);
  Register #(.width(32)) register_1 (.D(Data_In_0), .en(Chip_Select), .Q(register_1_q), .clk(CLK), .clr(or_5_out));
  or or_5 (or_5_out, ~Chip_Select, Reset);  // OR_Gate
  Register #(.width(32)) register_2 (.D(Data_In_1), .en(Chip_Select), .Q(register_2_q), .clk(CLK), .clr(or_6_out));
  or or_6 (or_6_out, ~Chip_Select, Reset);  // OR_Gate
  Register #(.width(32)) register_3 (.D(Data_In_2), .en(Chip_Select), .Q(register_3_q), .clk(CLK), .clr(or_7_out));
  or or_7 (or_7_out, ~Chip_Select, Reset);  // OR_Gate
  Register #(.width(32)) register_4 (.D(Data_In_3), .en(Chip_Select), .Q(register_4_q), .clk(CLK), .clr(or_8_out));
  or or_8 (or_8_out, ~Chip_Select, Reset);  // OR_Gate
  Register #(.width(32)) register_5 (
    .D({{11{1'b1}}, nRead_Write, Mask, Address}), .en(Chip_Select), .Q(register_5_q), .clk(CLK),
    .clr(or_9_out));
  or or_9 (or_9_out, ~Chip_Select, Reset);  // OR_Gate
  D_Flip_Flop Proc (.clk(CLK), .D(or_4_out), .Q(Proc_q), .reset(or_10_out));  // open: Qn, preset, en
  or or_10 (or_10_out, ~Chip_Select, Reset);  // OR_Gate
  Demultiplexer #(.enable("false")) demultiplexer_2 (
    .out0(Count), .out1(Update_Mem), .in(demultiplexer_3_out0), .sel(Zero_Time));
  Demultiplexer #(.enable("false")) demultiplexer_3 (
    .out0(demultiplexer_3_out0), .out1(Load1), .in(Proc_q), .sel(Changed));
  Clock clock_1 (.out(CLK));
  Comparator_part #(.width(32)) comparator_2 (.a(register_1_q), .b(Data_In_0), .eq(comparator_2_eq));  // open: gt, lt
  Comparator_part #(.width(32)) comparator_3 (.a(register_2_q), .b(Data_In_1), .eq(comparator_3_eq));  // open: gt, lt
  Comparator_part #(.width(32)) comparator_4 (.a(register_3_q), .b(Data_In_2), .eq(comparator_4_eq));  // open: gt, lt
  Comparator_part #(.width(32)) comparator_5 (.a(register_4_q), .b(Data_In_3), .eq(comparator_5_eq));  // open: gt, lt
  Comparator_part #(.width(32)) comparator_6 (
    .a(register_5_q), .b({{11{1'b1}}, nRead_Write, Mask, Address}), .eq(comparator_6_eq));  // open: gt, lt
  nand nand_1 (nand_1_out, comparator_6_eq, comparator_2_eq, comparator_3_eq, comparator_4_eq, comparator_5_eq);
  and and_1 (Changed, nand_1_out, Chip_Select);
  or or_11 (Load, Count, Load1, Load0);
  and and_2 (and_2_out, Mask[0], Update_Mem, nRead_Write);
  and and_3 (and_3_out, Mask[1], Update_Mem, nRead_Write);
  and and_4 (and_4_out, Mask[2], Update_Mem, nRead_Write);
  and and_5 (and_5_out, Mask[3], Update_Mem, nRead_Write);
  RAM_part #(.addrWidth(16), .dataWidth(32), .bus("separate")) ram_1 (
    .addr(Address), .din(Data_In_0), .data(Data_Out_0), .str(and_2_out), .sel(Chip_Select), .clk(CLK),
    .ld(and_6_out), .clr(Reset));
  and and_6 (and_6_out, ~nRead_Write, Idle);  // AND_Gate
  RAM_part #(.addrWidth(16), .dataWidth(32), .bus("separate")) ram_2 (
    .addr(Address), .din(Data_In_1), .data(Data_Out_1), .str(and_3_out), .sel(Chip_Select), .clk(CLK),
    .ld(and_7_out), .clr(Reset));
  and and_7 (and_7_out, ~nRead_Write, Idle);  // AND_Gate
  RAM_part #(.addrWidth(16), .dataWidth(32), .bus("separate")) ram_3 (
    .addr(Address), .din(Data_In_2), .data(Data_Out_2), .str(and_4_out), .sel(Chip_Select), .clk(CLK),
    .ld(and_8_out), .clr(Reset));
  and and_8 (and_8_out, ~nRead_Write, Idle);  // AND_Gate
  RAM_part #(.addrWidth(16), .dataWidth(32), .bus("separate")) ram_4 (
    .addr(Address), .din(Data_In_3), .data(Data_Out_3), .str(and_5_out), .sel(Chip_Select), .clk(CLK),
    .ld(and_9_out), .clr(Reset));
  and and_9 (and_9_out, ~nRead_Write, Idle);  // AND_Gate

  assign Read_Time = 4'b0011;
  assign Write_Time = 4'b0010;

  // Other names for the same wires on the sheet: M0 = Mask[0]; M1 = Mask[1]; M2 = Mask[2]; M3 = Mask[3];
  //   RW = nRead_Write; CLR = Reset; CS = Chip_Select; Load2 = Count

  // Notes on the sheet:
  //   NO MODIFICAR
  //   excepto quizás los valores RT y WT
  //   BANK0
  //   BANK1
  //   BANK2
  //   BANK3
endmodule

module S_MIPS (
  input  Kbd_Available,
  input  [6:0] Kbd_ASCII_Data,
  input  [31:0] RAM_Out_0,
  input  [31:0] RAM_Out_1,
  input  Reset,
  input  [31:0] RAM_Out_2,
  input  Clock,
  input  [31:0] RAM_Out_3,
  input  [3:0] Read_Time,
  input  [3:0] Write_Time,
  output Kbd_Enable,
  output [15:0] Address,
  output Kbd_Clear,
  output TTY_Enable,
  output [6:0] TTY_ASCII_Data,
  output Stop,
  output [31:0] RAM_In_0,
  output [31:0] RAM_In_1,
  output [31:0] RAM_In_2,
  output [31:0] RAM_In_3,
  output [3:0] Mask,
  output nRead_Write,
  output Chip_Select
);

  wire AluInst, d_ff_2_q, enGI, enPC, enRF, getData, getIsnt, Halt, JmpInst, MemInst, or_1_out, or_2_out,
       ReadyData, ReadyInst, ReadyW, RInst, StackInst, Start, Tty, Write, WriteInst;
  wire [31:0] Adderss, data_path_1_rout, DataIn, multiplexer_1_out, multiplexer_2_out, multiplexer_3_out,
       multiplexer_4_out, ram_interaction_1_out_14, ram_interaction_1_out_15, ram_interaction_1_out_16,
       ram_interaction_1_out_17;

  Multiplexer #(.width(32)) multiplexer_1 (
    .in0(RAM_Out_0), .in1(RAM_In_0), .out(multiplexer_1_out), .sel(Write));  // open: en
  Multiplexer #(.width(32)) multiplexer_2 (
    .in0(RAM_Out_1), .in1(RAM_In_0), .out(multiplexer_2_out), .sel(Write));  // open: en
  Multiplexer #(.width(32)) multiplexer_3 (
    .in0(RAM_Out_2), .in1(RAM_In_0), .out(multiplexer_3_out), .sel(Write));  // open: en
  Multiplexer #(.width(32)) multiplexer_4 (
    .in0(RAM_Out_3), .in1(RAM_In_0), .out(multiplexer_4_out), .sel(Write));  // open: en
  D_Flip_Flop #(.trigger("falling")) d_ff_1 (.clk(Clock), .D(Reset), .Q(Start));  // open: Qn, preset, en, reset
  RAM_Interaction ram_interaction_1 (
    .in_1(multiplexer_1_out), .in_2(multiplexer_2_out), .in_3(multiplexer_3_out), .in_4(multiplexer_4_out),
    .in_5(Adderss), .in_6(Read_Time), .in_7(Write_Time), .in_8(Clock), .in_9(Reset), .in_10(Write),
    .in_11(getIsnt), .in_12(getData), .in_13(enGI), .out_14(ram_interaction_1_out_14),
    .out_15(ram_interaction_1_out_15), .out_16(ram_interaction_1_out_16), .out_17(ram_interaction_1_out_17),
    .out_18(Address), .out_19(Mask), .out_20(nRead_Write), .out_21(Chip_Select), .out_22(ReadyInst),
    .out_23(ReadyData), .out_24(ReadyW));
  D_Flip_Flop #(.trigger("falling")) d_ff_2 (
    .clk(Clock), .D(getIsnt), .Q(d_ff_2_q), .en(or_1_out));  // open: Qn, preset, reset
  or or_1 (or_1_out, getIsnt, ReadyInst);
  or or_2 (or_2_out, StackInst, MemInst);
  Multiplexer #(.select(2), .width(32)) multiplexer_5 (
    .in0(ram_interaction_1_out_14), .in1(ram_interaction_1_out_15), .in2(ram_interaction_1_out_16),
    .in3(ram_interaction_1_out_17), .out(DataIn), .sel(Adderss[3:2]));  // open: en
  Control_Unit control_unit_1 (
    .in_1(Clock), .in_2(Start), .in_3(ReadyInst), .in_4(AluInst), .in_5(RInst), .in_6(Reset), .in_7(Tty),
    .in_8(ReadyData), .in_9(JmpInst), .in_10(or_2_out), .in_11(WriteInst), .in_12(ReadyW), .out_13(enRF),
    .out_14(enPC), .out_15(Stop), .out_16(getData), .out_18(enGI), .out_21(Write), .out_19(TTY_Enable),
    .out_17(getIsnt), .out_20(Kbd_Enable));
  Data_Path data_path_1 (
    .in_1(Clock), .in_2(Reset), .in_3(Kbd_Available), .in_4(d_ff_2_q), .in_5(enRF), .in_6(enPC),
    .in_8(DataIn), .out_11(Halt), .out_12(AluInst), .out_13(RInst), .out_14(JmpInst), .in_9(Kbd_ASCII_Data),
    .out_15(Tty), .out_16(MemInst), .out_17(StackInst), .out_18(WriteInst), .Address(Adderss),
    .TtyData(TTY_ASCII_Data), .ROut(data_path_1_rout), .in_7(enGI));
  InOut inout_1 (.in_1(data_path_1_rout), .Output(RAM_In_0));

  assign Kbd_Clear = Reset;
  assign RAM_In_1 = RAM_In_0;
  assign RAM_In_2 = RAM_In_0;
  assign RAM_In_3 = RAM_In_0;

  // Other names for the same wires on the sheet: CLK = Clock; CS = Chip_Select; KBD_AVAIL = Kbd_Available;
  //   CLR = Reset; KBD_CLR = Reset; KBD_DATA[6:0] = Kbd_ASCII_Data; RAM_A[15:0] = Address; RAM_MASK[3:0] = Mask;
  //   RAM_OUTPUT_0[31:0] = RAM_Out_0; RAM_OUTPUT_1[31:0] = RAM_Out_1; RAM_OUTPUT_2[31:0] = RAM_Out_2;
  //   RAM_OUTPUT_3[31:0] = RAM_Out_3; RAM_INPUT_0[31:0] = RAM_In_0; RAM_INPUT_1[31:0] = RAM_In_0;
  //   RAM_INPUT_2[31:0] = RAM_In_0; RAM_INPUT_3[31:0] = RAM_In_0; ROut[31:0] = RAM_In_0; RW = nRead_Write;
  //   TTY_DATA[6:0] = TTY_ASCII_Data

  // Notes on the sheet:
  //   RAM ADDRESS
  //   DATA FROM RAM
  //   DATA TO RAM
  //   DATA WRITE MASK
  //   RAM TIMING
  //   RAM CONTROL
  //   KEYBOARD
  //   TTY
  //   SEQUENCING
endmodule

module RAM_Dispatcher (
  input  [3:0] WriteTime,
  input  Clock,
  input  CLR,
  output [31:0] Data,
  output [15:0] Address,
  output [3:0] Mask,
  output Finished,
  output Write
);

  wire demultiplexer_2_out1, demultiplexer_3_out1, End, IDLE_q, IncAddr, Load, or_1_out, or_2_out, While_q,
       WriteEnd;
  wire [3:0] counter_1_q;
  wire [31:0] CurrentAddress_q;

  Counter #(.width(32), .max('hffffffff)) CurrentAddress (
    .count(IncAddr), .Q({CurrentAddress_q[31:18], Address, CurrentAddress_q[1:0]}), .clk(Clock), .clr(CLR));  // open: load, D, carry
  or or_1 (or_1_out, IncAddr, demultiplexer_3_out1, Finished);
  D_Flip_Flop IDLE (.clk(Clock), .D(or_1_out), .Q(IDLE_q), .preset(CLR));  // open: Qn, en, reset
  Demultiplexer #(.enable("false")) demultiplexer_1 (.out0(Load), .out1(Finished), .in(IDLE_q), .sel(End));
  D_Flip_Flop While (.clk(Clock), .D(or_2_out), .Q(While_q), .reset(CLR));  // open: Qn, preset, en
  or or_2 (or_2_out, Write, Load);
  RAM_part #(.addrWidth(18), .dataWidth(32)) ram_1 (
    .addr({Address, CurrentAddress_q[1:0]}), .data(Data), .clk(Clock));  // open: sel, ld, clr
  Demultiplexer #(.enable("false")) demultiplexer_2 (
    .out0(Write), .out1(demultiplexer_2_out1), .in(While_q), .sel(WriteEnd));
  Decoder #(.select(2)) decoder_1 (
    .out0(Mask[0]), .out1(Mask[1]), .out2(Mask[2]), .out3(Mask[3]), .sel(CurrentAddress_q[1:0]));  // open: en
  Demultiplexer #(.enable("false")) demultiplexer_3 (
    .out0(IncAddr), .out1(demultiplexer_3_out1), .in(demultiplexer_2_out1), .sel(End));
  Counter #(.width(4), .max('hf)) counter_1 (
    .load(Load), .D(WriteTime), .count(Write), .Q(counter_1_q), .clk(Clock));  // open: carry, clr
  Comparator_part #(.width(32)) comparator_1 (.a(Data), .b({32{1'b1}}), .eq(End));  // open: gt, lt
  Comparator_part #(.width(4)) comparator_2 (.a(4'b0000), .b(counter_1_q), .eq(WriteEnd));  // open: gt, lt

  // Other names for the same wires on the sheet: CLK = Clock; Count = Write; WT[3:0] = WriteTime
endmodule

// RF
module Register_File (
  input  in_1,
  input  in_2,
  input  [31:0] in_3,
  input  [4:0] in_4,
  input  [4:0] in_5,
  input  [4:0] in_6,
  input  in_7,
  input  in_8,
  input  in_9,
  input  in_10,
  output [31:0] OX,
  output [31:0] OY,
  output [31:0] SP
);

  wire In31, L0, L1, L2, L3, L4, L5, L6, L7, L8, L9, L10, L11, L12, L13, L14, L15, L16, L17, L18, L19, L20,
       L21, L22, L23, L24, L25, L26, L27, L28, L29, L30, L31, or_1_out, or_2_out, undriven;
  wire [31:0] adder_1_out, multiplexer_1_out, multiplexer_4_out, Out0, Out1, Out2, Out3, Out4, Out5, Out6,
       Out7, Out8, Out9, Out10, Out11, Out12, Out13, Out14, Out15, Out16, Out17, Out18, Out19, Out20, Out21,
       Out22, Out23, Out24, Out25, Out26, Out27, Out28, Out29, Out30, SP_t, subtractor_1_out;

  Demultiplexer #(.select(5)) demultiplexer_1 (
    .out0(L0), .out1(L1), .out2(L2), .out3(L3), .out4(L4), .out5(L5), .out6(L6), .out7(L7), .out8(L8),
    .out9(L9), .out10(L10), .out11(L11), .out12(L12), .out13(L13), .out14(L14), .out15(L15), .out16(L16),
    .out17(L17), .out18(L18), .out19(L19), .out20(L20), .out21(L21), .out22(L22), .out23(L23), .out24(L24),
    .out25(L25), .out26(L26), .out27(L27), .out28(L28), .out29(L29), .out30(L30), .out31(In31), .in(in_7),
    .sel(in_4), .en(undriven));
  or or_1 (or_1_out, in_9, in_10);
  and and_1 (L31, or_1_out, in_8);
  Subtractor #(.width(32)) subtractor_1 (.a(SP), .b(32'h4), .out(subtractor_1_out));  // open: bin, bout
  Adder #(.width(32)) adder_1 (.a(32'h4), .b(SP), .out(adder_1_out));  // open: cin, cout
  Multiplexer #(.width(32)) multiplexer_1 (
    .in0(subtractor_1_out), .in1(adder_1_out), .out(multiplexer_1_out), .sel(in_10));  // open: en
  Multiplexer #(.width(32)) multiplexer_2 (
    .in0(multiplexer_1_out), .in1({32{1'b1}}), .out(SP_t), .sel(in_2));  // open: en
  Register #(.width(32)) register_1 (.D({32{1'b0}}), .en(L0), .Q(Out0), .clk(in_1), .clr(in_2));
  Register #(.width(32)) register_2 (.D(in_3), .en(L6), .Q(Out6), .clk(in_1), .clr(in_2));
  Register #(.width(32)) register_3 (.D(in_3), .en(L12), .Q(Out12), .clk(in_1), .clr(in_2));
  Register #(.width(32)) register_4 (.D(in_3), .en(L18), .Q(Out18), .clk(in_1), .clr(in_2));
  Register #(.width(32)) register_5 (.D(in_3), .en(L24), .Q(Out24), .clk(in_1), .clr(in_2));
  Register #(.width(32)) register_6 (.D(in_3), .en(L30), .Q(Out30), .clk(in_1), .clr(in_2));
  Register #(.width(32)) register_7 (.D(in_3), .en(L1), .Q(Out1), .clk(in_1), .clr(in_2));
  Register #(.width(32)) register_8 (.D(in_3), .en(L7), .Q(Out7), .clk(in_1), .clr(in_2));
  Register #(.width(32)) register_9 (.D(in_3), .en(L13), .Q(Out13), .clk(in_1), .clr(in_2));
  Register #(.width(32)) register_10 (.D(in_3), .en(L19), .Q(Out19), .clk(in_1), .clr(in_2));
  Register #(.width(32)) register_11 (.D(in_3), .en(L25), .Q(Out25), .clk(in_1), .clr(in_2));
  Multiplexer #(.select(5), .width(32)) multiplexer_3 (
    .in0(Out0), .in1(Out1), .in2(Out2), .in3(Out3), .in4(Out4), .in5(Out5), .in6(Out6), .in7(Out7),
    .in8(Out8), .in9(Out9), .in10(Out10), .in11(Out11), .in12(Out12), .in13(Out13), .in14(Out14),
    .in15(Out15), .in16(Out16), .in17(Out17), .in18(Out18), .in19(Out19), .in20(Out20), .in21(Out21),
    .in22(Out22), .in23(Out23), .in24(Out24), .in25(Out25), .in26(Out26), .in27(Out27), .in28(Out28),
    .in29(Out29), .in30(Out30), .in31(SP), .out(OX), .sel(in_5));  // open: en
  Register #(.width(32)) register_12 (.D(in_3), .en(L2), .Q(Out2), .clk(in_1), .clr(in_2));
  Register #(.width(32)) register_13 (.D(in_3), .en(L8), .Q(Out8), .clk(in_1), .clr(in_2));
  Register #(.width(32)) register_14 (.D(in_3), .en(L14), .Q(Out14), .clk(in_1), .clr(in_2));
  Register #(.width(32)) register_15 (.D(in_3), .en(L20), .Q(Out20), .clk(in_1), .clr(in_2));
  Register #(.width(32)) register_16 (.D(in_3), .en(L26), .Q(Out26), .clk(in_1), .clr(in_2));
  Register #(.width(32)) register_17 (.D(in_3), .en(L3), .Q(Out3), .clk(in_1), .clr(in_2));
  Register #(.width(32)) register_18 (.D(in_3), .en(L9), .Q(Out9), .clk(in_1), .clr(in_2));
  Register #(.width(32)) register_19 (.D(in_3), .en(L15), .Q(Out15), .clk(in_1), .clr(in_2));
  Register #(.width(32)) register_20 (.D(in_3), .en(L21), .Q(Out21), .clk(in_1), .clr(in_2));
  Register #(.width(32)) register_21 (.D(in_3), .en(L27), .Q(Out27), .clk(in_1), .clr(in_2));
  Multiplexer #(.width(32)) multiplexer_4 (.in0(SP_t), .in1(in_3), .out(multiplexer_4_out), .sel(In31));  // open: en
  Register #(.width(32)) register_22 (.D(in_3), .en(L4), .Q(Out4), .clk(in_1), .clr(in_2));
  Register #(.width(32)) register_23 (.D(in_3), .en(L10), .Q(Out10), .clk(in_1), .clr(in_2));
  Register #(.width(32)) register_24 (.D(in_3), .en(L16), .Q(Out16), .clk(in_1), .clr(in_2));
  Register #(.width(32)) register_25 (.D(in_3), .en(L22), .Q(Out22), .clk(in_1), .clr(in_2));
  Register #(.width(32)) register_26 (.D(in_3), .en(L28), .Q(Out28), .clk(in_1), .clr(in_2));
  Multiplexer #(.select(5), .width(32)) multiplexer_5 (
    .in0(Out0), .in1(Out1), .in2(Out2), .in3(Out3), .in4(Out4), .in5(Out5), .in6(Out6), .in7(Out7),
    .in8(Out8), .in9(Out9), .in10(Out10), .in11(Out11), .in12(Out12), .in13(Out13), .in14(Out14),
    .in15(Out15), .in16(Out16), .in17(Out17), .in18(Out18), .in19(Out19), .in20(Out20), .in21(Out21),
    .in22(Out22), .in23(Out23), .in24(Out24), .in25(Out25), .in26(Out26), .in27(Out27), .in28(Out28),
    .in29(Out29), .in30(Out30), .in31(SP), .out(OY), .sel(in_6));  // open: en
  or or_2 (or_2_out, L31, In31, in_2);
  Register #(.width(32)) register_27 (.D(in_3), .en(L5), .Q(Out5), .clk(in_1), .clr(in_2));
  Register #(.width(32)) register_28 (.D(in_3), .en(L11), .Q(Out11), .clk(in_1), .clr(in_2));
  Register #(.width(32)) register_29 (.D(in_3), .en(L17), .Q(Out17), .clk(in_1), .clr(in_2));
  Register #(.width(32)) register_30 (.D(in_3), .en(L23), .Q(Out23), .clk(in_1), .clr(in_2));
  Register #(.width(32)) register_31 (.D(in_3), .en(L29), .Q(Out29), .clk(in_1), .clr(in_2));
  Register #(.width(32)) register_32 (.D(multiplexer_4_out), .en(or_2_out), .Q(SP), .clk(in_1));  // open: clr

  // Other names for the same wires on the sheet: Clk = in_1; enPC = in_8; In[31:0] = in_3; Out31[31:0] = SP;
  //   Pop = in_10; Push = in_9; Reset = in_2; Select[4:0] = in_4; SX[4:0] = in_5; SY[4:0] = in_6; W = in_7;
  //   X[31:0] = OX; Y[31:0] = OY
endmodule

// RFin
module RF_Input (
  input  [31:0] in_1,
  input  [31:0] in_2,
  input  [31:0] in_3,
  input  [31:0] in_4,
  input  [31:0] in_5,
  input  [6:0] in_6,
  input  in_7,
  input  in_8,
  input  in_9,
  input  in_10,
  input  in_11,
  input  in_12,
  output [31:0] out_13
);

  wire [2:0] Select;
  wire [31:0] Kdb;

  or or_1 (Select[0], in_7, in_8, in_10, in_11);
  or or_2 (Select[1], in_9, in_10);
  or or_3 (Select[2], in_12, in_11);
  Multiplexer #(.select(3), .width(32)) multiplexer_1 (
    .in0(in_1), .in1(in_3), .in2(in_4), .in3(in_5), .in4(in_2), .in5(Kdb), .out(out_13), .sel(Select));  // open: in6, in7, en

  // Other names for the same wires on the sheet: ALU[31:0] = in_1; HI[31:0] = in_4; isKbd = in_11; isRnd = in_12;
  //   Kbd[6:0] = in_6; LO[31:0] = in_5; Lw = in_7; MemX[31:0] = in_3; Mfhi = in_9; Mflo = in_10; OUT[31:0] = out_13;
  //   Pop = in_8; RND[31:0] = in_2
endmodule

module ALU (
  input  [31:0] X,
  input  [31:0] Y,
  input  [3:0] in_3,
  input  in_4,
  input  in_5,
  output [31:0] OUT,
  output [31:0] OH,
  output [31:0] OL
);

  wire and_3_out, comparator_1_comp, Enable, mult;
  wire [31:0] ADD, AND, Div, DivRem, MultH, multiplexer_1_out, multiplexer_2_out, MultL, NOR, OR, SLT, SUB,
       XOR;

  Adder #(.width(32)) adder_1 (.a(X), .b(Y), .out(ADD));  // open: cin, cout
  Subtractor #(.width(32)) subtractor_1 (.a(X), .b(Y), .out(SUB));  // open: bin, bout
  assign AND = X & Y;  // AND_Gate and_1, 32 bits wide
  assign OR = X | Y;  // OR_Gate or_1, 32 bits wide
  assign NOR = ~(X | Y);  // NOR_Gate nor_1, 32 bits wide
  assign XOR = X ^ Y;  // XOR_Gate xor_1, 32 bits wide
  Comparator comparator_1 (.in_1(X), .in_2(Y), .in_3(in_5), .Comp(comparator_1_comp));
  assign SLT = {{31{1'b0}}, comparator_1_comp};  // Bit_Extender bit_extender_1
  Multiplication multiplication_1 (.in_1(in_5), .X(X), .Y(Y), .OH(MultH), .OL(MultL));
  Division division_1 (.in_2(X), .in_3(Y), .DivRem(DivRem), .Div(Div), .in_1(in_5));
  and and_2 (mult, ~in_3[0], in_3[1], ~in_3[2], ~in_3[3]);  // AND_Gate
  and and_3 (and_3_out, in_3[0], in_3[1], ~in_3[2], ~in_3[3]);  // AND_Gate
  Multiplexer #(.width(32)) multiplexer_1 (.in0(DivRem), .in1(MultH), .out(multiplexer_1_out), .sel(mult));  // open: en
  or or_2 (Enable, mult, and_3_out);
  Register #(.width(32)) register_1 (.D(multiplexer_1_out), .en(Enable), .Q(OH), .clk(in_4));  // open: clr
  Multiplexer #(.width(32)) multiplexer_2 (.in0(Div), .in1(MultL), .out(multiplexer_2_out), .sel(mult));  // open: en
  Multiplexer #(.select(4), .width(32)) multiplexer_3 (
    .in0(ADD), .in1(SUB), .in4(SLT), .in5(AND), .in6(OR), .in7(NOR), .in8(XOR), .out(OUT), .sel(in_3));  // open: in2, in3, in9, in10, in11, in12, in13, in14, in15, en
  Register #(.width(32)) register_2 (.D(multiplexer_2_out), .en(Enable), .Q(OL), .clk(in_4));  // open: clr

  // Other names for the same wires on the sheet: Clk = in_4; Select[3:0] = in_3; Sign = in_5
endmodule

// ALUSelect
module ALU_Select (
  input  in_1,
  input  in_2,
  input  in_3,
  input  in_4,
  input  in_5,
  input  in_6,
  input  in_7,
  input  in_8,
  input  in_9,
  input  in_10,
  input  in_11,
  input  in_12,
  input  in_13,
  input  in_14,
  input  in_15,
  input  in_16,
  input  in_17,
  input  in_18,
  output Sign,
  output I,
  output [3:0] Select
);

  wire AND, DIV, MULT, OR, SLT, SLTI;

  or or_1 (Select[0], DIV, AND, in_4, in_8);
  or or_2 (Select[1], DIV, OR, MULT, in_8);
  or or_3 (Sign, in_11, in_7, in_15, in_14);
  or or_4 (Select[2], SLT, AND, SLTI, OR, in_8);
  or or_5 (I, in_14, in_12, in_18, in_6, in_3);
  or or_6 (DIV, in_11, in_13);
  or or_7 (MULT, in_7, in_9);
  or or_8 (SLT, in_15, in_17);
  or or_9 (SLTI, in_14, in_16);
  or or_10 (AND, in_2, in_18);
  or or_11 (OR, in_5, in_3);
  or or_12 (Select[3], in_10, in_6);

  // Other names for the same wires on the sheet: Add = in_1; Addi = in_12; And_t = in_2; Andi = in_18; Div_t = in_11;
  //   Divu = in_13; Mult_t = in_7; Mulu = in_9; Nor = in_8; Or_t = in_5; Ori = in_3; _0 = Select[0]; _1 = Select[1];
  //   _2 = Select[2]; _3 = Select[3]; XOR = Select[3]; Slt_t = in_15; Slti_t = in_14; Sltiu = in_16; Sltu = in_17;
  //   Sub = in_4; Xor_t = in_10; Xori = in_6
endmodule

// Instruction Decoder
module Instruction_Decoder (
  input  [31:0] in_1,
  output out_2,
  output out_3,
  output out_4,
  output out_5,
  output [4:0] out_6,
  output out_7,
  output out_8,
  output out_9,
  output out_10,
  output [25:0] out_11,
  output [4:0] out_12,
  output out_13,
  output out_14,
  output out_15,
  output out_16,
  output [4:0] out_17,
  output out_18,
  output out_19,
  output out_20,
  output out_21,
  output [15:0] out_22,
  output out_23,
  output out_24,
  output out_25,
  output out_26,
  output out_27,
  output out_28,
  output out_29,
  output out_30,
  output out_31,
  output out_32,
  output out_33,
  output out_34,
  output out_35,
  output out_36,
  output out_37,
  output out_38,
  output out_39,
  output out_40,
  output out_41,
  output out_42
);

  wire _000000, _111111, comparator_17_eq, comparator_18_eq, comparator_19_eq, comparator_20_eq,
       comparator_21_eq, comparator_22_eq, comparator_23_eq, comparator_24_eq, comparator_25_eq,
       comparator_26_eq, comparator_27_eq, comparator_28_eq, comparator_29_eq, comparator_30_eq,
       comparator_31_eq, comparator_32_eq, comparator_33_eq, comparator_34_eq, comparator_35_eq,
       comparator_36_eq, comparator_37_eq, comparator_38_eq, comparator_39_eq, comparator_40_eq;

  Comparator_part #(.width(6)) comparator_1 (.a(in_1[31:26]), .b({6{1'b1}}), .eq(_111111));  // open: gt, lt
  Comparator_part #(.width(6)) comparator_2 (.a(in_1[31:26]), .b({6{1'b0}}), .eq(_000000));  // open: gt, lt
  Comparator_part #(.width(6)) comparator_3 (.a(in_1[31:26]), .b(6'b001000), .eq(out_5));  // open: gt, lt
  Comparator_part #(.width(6)) comparator_4 (.a(in_1[31:26]), .b(6'b001010), .eq(out_10));  // open: gt, lt
  Comparator_part #(.width(6)) comparator_5 (.a(in_1[31:26]), .b(6'b001011), .eq(out_16));  // open: gt, lt
  Comparator_part #(.width(6)) comparator_6 (.a(in_1[31:26]), .b(6'b001100), .eq(out_21));  // open: gt, lt
  Comparator_part #(.width(6)) comparator_7 (.a(in_1[31:26]), .b(6'b001101), .eq(out_26));  // open: gt, lt
  Comparator_part #(.width(6)) comparator_8 (.a(in_1[31:26]), .b(6'b001110), .eq(out_30));  // open: gt, lt
  Comparator_part #(.width(6)) comparator_9 (.a(in_1[31:26]), .b(6'b100011), .eq(out_4));  // open: gt, lt
  Comparator_part #(.width(6)) comparator_10 (.a(in_1[31:26]), .b(6'b101011), .eq(out_9));  // open: gt, lt
  Comparator_part #(.width(6)) comparator_11 (.a(in_1[31:26]), .b(6'b000100), .eq(out_15));  // open: gt, lt
  Comparator_part #(.width(6)) comparator_12 (.a(in_1[31:26]), .b(6'b000101), .eq(out_20));  // open: gt, lt
  Comparator_part #(.width(6)) comparator_13 (.a(in_1[31:26]), .b(6'b000110), .eq(out_25));  // open: gt, lt
  Comparator_part #(.width(6)) comparator_14 (.a(in_1[31:26]), .b(6'b000111), .eq(out_29));  // open: gt, lt
  Comparator_part #(.width(6)) comparator_15 (.a(in_1[31:26]), .b(6'b000001), .eq(out_35));  // open: gt, lt
  Comparator_part #(.width(6)) comparator_16 (.a(in_1[31:26]), .b(6'b000010), .eq(out_40));  // open: gt, lt
  Comparator_part #(.width(6)) comparator_17 (.a(in_1[5:0]), .b({6{1'b0}}), .eq(comparator_17_eq));  // open: gt, lt
  Comparator_part #(.width(6)) comparator_18 (.a(in_1[5:0]), .b(6'b100000), .eq(comparator_18_eq));  // open: gt, lt
  Comparator_part #(.width(6)) comparator_19 (.a(in_1[5:0]), .b(6'b100010), .eq(comparator_19_eq));  // open: gt, lt
  Comparator_part #(.width(6)) comparator_20 (.a(in_1[5:0]), .b(6'b011000), .eq(comparator_20_eq));  // open: gt, lt
  Comparator_part #(.width(6)) comparator_21 (.a(in_1[5:0]), .b(6'b011001), .eq(comparator_21_eq));  // open: gt, lt
  Comparator_part #(.width(6)) comparator_22 (.a(in_1[5:0]), .b(6'b011010), .eq(comparator_22_eq));  // open: gt, lt
  Comparator_part #(.width(6)) comparator_23 (.a(in_1[5:0]), .b(6'b011011), .eq(comparator_23_eq));  // open: gt, lt
  Comparator_part #(.width(6)) comparator_24 (.a(in_1[5:0]), .b(6'b101010), .eq(comparator_24_eq));  // open: gt, lt
  and and_1 (out_2, _000000, comparator_17_eq);
  and and_2 (out_7, _000000, comparator_18_eq);
  and and_3 (out_13, _000000, comparator_19_eq);
  and and_4 (out_18, _000000, comparator_20_eq);
  and and_5 (out_23, _000000, comparator_21_eq);
  and and_6 (out_27, _000000, comparator_22_eq);
  and and_7 (out_33, _000000, comparator_23_eq);
  and and_8 (out_38, _000000, comparator_24_eq);
  Comparator_part #(.width(6)) comparator_25 (.a(in_1[5:0]), .b(6'b101011), .eq(comparator_25_eq));  // open: gt, lt
  Comparator_part #(.width(6)) comparator_26 (.a(in_1[5:0]), .b(6'b100100), .eq(comparator_26_eq));  // open: gt, lt
  Comparator_part #(.width(6)) comparator_27 (.a(in_1[5:0]), .b(6'b100101), .eq(comparator_27_eq));  // open: gt, lt
  Comparator_part #(.width(6)) comparator_28 (.a(in_1[5:0]), .b(6'b100111), .eq(comparator_28_eq));  // open: gt, lt
  Comparator_part #(.width(6)) comparator_29 (.a(in_1[5:0]), .b(6'b101000), .eq(comparator_29_eq));  // open: gt, lt
  Comparator_part #(.width(6)) comparator_30 (.a(in_1[5:0]), .b(6'b001000), .eq(comparator_30_eq));  // open: gt, lt
  Comparator_part #(.width(6)) comparator_31 (.a(in_1[5:0]), .b(6'b010000), .eq(comparator_31_eq));  // open: gt, lt
  Comparator_part #(.width(6)) comparator_32 (.a(in_1[5:0]), .b(6'b010010), .eq(comparator_32_eq));  // open: gt, lt
  and and_9 (out_3, _000000, comparator_25_eq);
  and and_10 (out_8, _000000, comparator_26_eq);
  and and_11 (out_14, _000000, comparator_27_eq);
  and and_12 (out_19, _000000, comparator_28_eq);
  and and_13 (out_24, _000000, comparator_29_eq);
  and and_14 (out_28, _000000, comparator_30_eq);
  and and_15 (out_34, _000000, comparator_31_eq);
  and and_16 (out_39, _000000, comparator_32_eq);
  and and_17 (out_31, _111111, comparator_33_eq);
  Comparator_part #(.width(6)) comparator_33 (.a(in_1[5:0]), .b({6{1'b1}}), .eq(comparator_33_eq));  // open: gt, lt
  and and_18 (out_37, _111111, comparator_34_eq);
  Comparator_part #(.width(6)) comparator_34 (.a(in_1[5:0]), .b(6'b000001), .eq(comparator_34_eq));  // open: gt, lt
  and and_19 (out_42, _111111, comparator_35_eq);
  Comparator_part #(.width(6)) comparator_35 (.a(in_1[5:0]), .b(6'b000010), .eq(comparator_35_eq));  // open: gt, lt
  Comparator_part #(.width(6)) comparator_36 (.a(in_1[31:26]), .b(6'b111000), .eq(comparator_36_eq));  // open: gt, lt
  Comparator_part #(.width(6)) comparator_37 (.a(in_1[5:0]), .b({6{1'b0}}), .eq(comparator_37_eq));  // open: gt, lt
  Comparator_part #(.width(6)) comparator_38 (.a(in_1[31:26]), .b(6'b111000), .eq(comparator_38_eq));  // open: gt, lt
  Comparator_part #(.width(6)) comparator_39 (.a(in_1[5:0]), .b(6'b000001), .eq(comparator_39_eq));  // open: gt, lt
  and and_20 (out_32, _111111, comparator_40_eq);
  Comparator_part #(.width(6)) comparator_40 (.a(in_1[5:0]), .b(6'b000100), .eq(comparator_40_eq));  // open: gt, lt
  and and_21 (out_36, comparator_36_eq, comparator_37_eq);
  and and_22 (out_41, comparator_38_eq, comparator_39_eq);

  assign out_6 = in_1[25:21];
  assign out_11 = in_1[25:0];
  assign out_12 = in_1[20:16];
  assign out_17 = in_1[15:11];
  assign out_22 = in_1[15:0];

  // Other names for the same wires on the sheet: Add = out_7; Addi = out_5; And = out_8; Andi = out_21; Bgtz = out_29;
  //   Blez = out_25; Bltz = out_35; Bne = out_20; Bqe = out_15; Const[15:0] = in_1[15:0]; Dest[25:0] = in_1[25:0];
  //   FC[5:0] = in_1[5:0]; RD[4:0] = in_1[15:11]; RT[4:0] = in_1[20:16]; RS[4:0] = in_1[25:21]; Div = out_27;
  //   Divu = out_33; Halt = out_31; J = out_40; Jr = out_28; Kbd = out_32; Lw = out_4; Mfhi = out_34; Mflo = out_39;
  //   Mult = out_18; Mulu = out_23; Nop = out_2; Nor = out_19; OP[5:0] = in_1[31:26]; Or = out_14; Ori = out_26;
  //   Pop = out_36; Push = out_41; Rnd = out_42; Slt = out_38; Slti = out_10; Sltiu = out_16; Sltu = out_3;
  //   Sub = out_13; Sw = out_9; Tty = out_37; Xor = out_24; Xori = out_30
endmodule

// Data Path
module Data_Path (
  input  in_1,
  input  in_2,
  input  in_3,
  input  in_4,
  input  in_5,
  input  in_6,
  input  in_7,
  input  [31:0] in_8,
  input  [6:0] in_9,
  output [31:0] ROut,
  output out_11,
  output out_12,
  output out_13,
  output out_14,
  output out_15,
  output out_16,
  output out_17,
  output out_18,
  output [6:0] TtyData,
  output [31:0] Address
);

  wire Add, Addi, And, Andi, Bgtz, Blez, Bltz, Bne, Bqe, Div, Divu, I, J, Jr, Kbd, Lw, Mfhi, Mflo, Mult,
       Mulu, Nop, Nor, Or, or_1_out, or_2_out, or_3_out, or_10_out, Ori, Pop, Push, Rnd, Sign, Slt, Slti,
       Sltiu, Sltu, Sub, Sw, Xor, Xori;
  wire [3:0] AluSelect;
  wire [4:0] multiplexer_1_out, RD, RS, RT;
  wire [15:0] Const;
  wire [25:0] Dest;
  wire [31:0] AluOut, HI, inout_1_output, LO, multiplexer_3_out, PCIn, PCOut, random_1_out, register_1_q,
       rf_input_1_out_13, RT_t, SP;
  wire [31:7] RS_t;
  wire [31:31] and_1_out;

  Random #(.width(32)) random_1 (.clk(in_1), .next(Rnd), .out(random_1_out));  // open: clr
  InOut inout_1 (.in_1(in_8), .Output(inout_1_output));
  Register #(.width(32)) register_1 (.D(inout_1_output), .en(in_7), .Q(register_1_q), .clk(in_1), .clr(in_2));
  or or_1 (or_1_out, Add, And, Ori, Sub, Or);
  or or_2 (or_2_out, Xori, Mult, Nor, Mulu, Xor, Div, Addi, Divu);
  or or_3 (or_3_out, Slti, Slt, Sltiu, Sltu, Andi);
  Instruction_Decoder instruction_decoder_1 (
    .out_2(Nop), .out_3(Sltu), .out_4(Lw), .out_5(Addi), .out_6(RS), .in_1(register_1_q), .out_7(Add),
    .out_8(And), .out_9(Sw), .out_10(Slti), .out_11(Dest), .out_12(RT), .out_13(Sub), .out_14(Or),
    .out_15(Bqe), .out_16(Sltiu), .out_17(RD), .out_18(Mult), .out_19(Nor), .out_20(Bne), .out_21(Andi),
    .out_22(Const), .out_23(Mulu), .out_24(Xor), .out_25(Blez), .out_26(Ori), .out_27(Div), .out_28(Jr),
    .out_29(Bgtz), .out_30(Xori), .out_33(Divu), .out_34(Mfhi), .out_35(Bltz), .out_38(Slt), .out_39(Mflo),
    .out_40(J), .out_36(Pop), .out_41(Push), .out_31(out_11), .out_37(out_15), .out_42(Rnd), .out_32(Kbd));
  RF_Input rf_input_1 (
    .in_1(AluOut), .in_2(random_1_out), .in_3(in_8), .in_4(HI), .in_5(LO), .in_6(in_9), .in_7(Lw),
    .in_8(Pop), .in_9(Mfhi), .in_10(Mflo), .in_11(Kbd), .in_12(Rnd), .out_13(rf_input_1_out_13));
  or or_4 (out_12, or_1_out, or_2_out, or_3_out);
  Multiplexer #(.width(5)) multiplexer_1 (.in0(RD), .in1(RT), .out(multiplexer_1_out), .sel(I));  // open: en
  Register_File register_file_1 (
    .in_3(rf_input_1_out_13), .in_4(multiplexer_1_out), .in_5(RS), .in_6(RT), .in_7(in_5), .in_8(in_6),
    .in_9(Push), .in_10(Pop), .OX({RS_t, TtyData}), .OY(RT_t), .in_1(in_1), .in_2(in_2), .SP(SP));
  or or_5 (out_13, Rnd, Mfhi, Mflo, Kbd, out_15);
  or or_6 (out_14, Bgtz, Bqe, Bne, Blez, Bltz, Jr, J, Nop);
  or or_7 (out_18, Push, Sw);
  or or_8 (out_17, Push, Pop);
  or or_9 (out_16, Lw, Sw);
  Branch_Control branch_control_1 (
    .in_1(Dest), .in_2({RS_t, TtyData}), .in_3(RT_t), .in_4(PCOut), .in_5(Const), .in_6(Bqe), .in_7(Bne),
    .in_8(Blez), .in_9(Bgtz), .in_10(Bltz), .in_11(Jr), .in_12(J), .OUT(PCIn));
  Memory_Adderss memory_adderss_1 (
    .in_1(PCOut), .in_2(AluOut), .in_3(SP), .in_4(Lw), .in_5(Sw), .in_6(Pop), .in_7(Push), .in_8(in_4),
    .OUT(Address));
  Multiplexer #(.width(32)) multiplexer_2 (.in0({RS_t, TtyData}), .in1(RT_t), .out(ROut), .sel(Sw));  // open: en
  or or_10 (or_10_out, Sw, Addi, Lw);
  and and_1 (and_1_out[31], ~Xori, ~Andi, ~Ori, Const[15]);  // AND_Gate
  Multiplexer #(.width(32)) multiplexer_3 (
    .in0(RT_t), .in1({{16{and_1_out[31]}}, Const}), .out(multiplexer_3_out), .sel(I));  // open: en
  PC pc_1 (.in_4(PCIn), .out_5(PCOut), .in_1(in_2), .in_2(in_1), .in_3(in_6));
  ALU_Select alu_select_1 (
    .in_1(Add), .in_2(And), .in_3(Ori), .in_4(Sub), .in_5(Or), .in_6(Xori), .in_7(Mult), .in_8(Nor),
    .in_9(Mulu), .in_10(Xor), .in_11(Div), .in_12(or_10_out), .in_13(Divu), .in_14(Slti), .in_15(Slt),
    .in_16(Sltiu), .in_17(Sltu), .in_18(Andi), .Sign(Sign), .Select(AluSelect), .I(I));
  ALU alu_1 (
    .X({RS_t, TtyData}), .Y(multiplexer_3_out), .in_3(AluSelect), .in_4(in_1), .in_5(Sign), .OUT(AluOut),
    .OH(HI), .OL(LO));

  // Other names for the same wires on the sheet: AluInst = out_12; Clk = in_1; enGI = in_7; enPC = in_6; enRF = in_5;
  //   Halt = out_11; Instruction[31:0] = in_8; JmpInst = out_14; KbdAva = in_3; KbdData[6:0] = in_9; MemInst = out_16;
  //   Nextl = in_4; Reset = in_2; RInst = out_13; RS_t[6:0] = TtyData; StackInst = out_17; Tty = out_15;
  //   WriteInst = out_18
endmodule

// CU
module Control_Unit (
  input  in_1,
  input  in_2,
  input  in_3,
  input  in_4,
  input  in_5,
  input  in_6,
  input  in_7,
  input  in_8,
  input  in_9,
  input  in_10,
  input  in_11,
  input  in_12,
  output out_13,
  output out_14,
  output out_15,
  output out_16,
  output out_17,
  output out_18,
  output out_19,
  output out_20,
  output out_21
);

  wire Branch, d_ff_1_q, d_ff_2_q, d_ff_3_q, d_ff_5_q, demultiplexer_1_out0, demultiplexer_1_out1, or_5_out,
       RF;
  wire [2:0] or_1_out;

  D_Flip_Flop #(.trigger("falling")) d_ff_1 (.clk(in_1), .D(in_2), .Q(d_ff_1_q), .reset(in_6));  // open: Qn, preset, en
  or or_1 (or_1_out[0], in_5, in_4, in_11);
  or or_2 (or_1_out[1], in_5, in_9);
  or or_3 (or_1_out[2], in_10, in_11);
  D_Flip_Flop #(.trigger("falling")) d_ff_2 (.clk(in_1), .D(in_3), .Q(d_ff_2_q));  // open: Qn, preset, en, reset
  D_Flip_Flop #(.trigger("falling")) d_ff_3 (
    .clk(in_1), .D(out_14), .Q(d_ff_3_q), .reset(in_6));  // open: Qn, preset, en
  Demultiplexer #(.select(3)) demultiplexer_1 (
    .out0(demultiplexer_1_out0), .out1(demultiplexer_1_out1), .out2(Branch), .out3(RF), .out4(out_16),
    .out5(out_21), .in(d_ff_2_q), .sel(or_1_out));  // open: out6, out7, en
  or or_4 (out_17, d_ff_1_q, d_ff_3_q);
  or or_5 (or_5_out, out_15, demultiplexer_1_out0);
  D_Flip_Flop #(.trigger("falling")) d_ff_4 (
    .clk(in_1), .D(or_5_out), .Q(out_15), .reset(in_6));  // open: Qn, preset, en
  D_Flip_Flop #(.trigger("falling")) d_ff_5 (
    .clk(in_1), .D(demultiplexer_1_out1), .Q(d_ff_5_q), .reset(in_6));  // open: Qn, preset, en
  or or_6 (out_13, d_ff_5_q, in_8, RF);
  D_Flip_Flop #(.trigger("falling")) d_ff_6 (.clk(in_1), .D(out_13), .Q(out_20));  // open: Qn, preset, en, reset
  or or_7 (out_14, out_20, in_12, Branch);
  and and_1 (out_19, out_20, in_7);

  assign out_18 = in_3;

  // Other names for the same wires on the sheet: AluInst = in_4; Clk = in_1; End = out_15; getData = out_16;
  //   getInst = out_17; JmpInst = in_9; MemInst = in_10; ReadyData = in_8; ReadyW = in_12; Reset = in_6; RInst = in_5;
  //   Start = in_2; KbdEn = out_20; Tty = out_20; TtyEn = out_19; TtyInst = in_7; ReadyInst = in_3; useGI = in_3;
  //   Cont = out_14; usePC = out_14; useRF = out_13; Write = out_21; WriteInst = in_11
endmodule

// RAM Iter
module RAM_Interaction (
  input  [31:0] in_1,
  input  [31:0] in_2,
  input  [31:0] in_3,
  input  [31:0] in_4,
  input  [31:0] in_5,
  input  [3:0] in_6,
  input  [3:0] in_7,
  input  in_8,
  input  in_9,
  input  in_10,
  input  in_11,
  input  in_12,
  input  in_13,
  output [31:0] out_14,
  output [31:0] out_15,
  output [31:0] out_16,
  output [31:0] out_17,
  output [15:0] out_18,
  output [3:0] out_19,
  output out_20,
  output out_21,
  output out_22,
  output out_23,
  output out_24
);

  wire CSD, CSI, or_1_out, Stop0;
  wire [31:0] DO0, DO1, DO2, DO3, inout_1_output, inout_2_output, inout_3_output, inout_4_output, IO0, IO1,
       IO2, IO3;

  or or_1 (or_1_out, in_10, Stop0);
  D_Flip_Flop #(.trigger("falling")) d_ff_1 (
    .clk(in_8), .D(in_10), .Q(out_20), .en(or_1_out));  // open: Qn, preset, reset
  Read_Ram read_ram_1 (
    .in_1(in_1), .in_2(in_2), .in_3(in_3), .in_4(in_4), .in_6(in_6), .in_7(in_8), .in_8(in_9), .in_9(in_11),
    .out_11(IO0), .out_12(IO1), .out_13(IO2), .out_14(IO3), .out_15(CSI), .out_16(out_22), .in_5(in_5[19:4]),
    .in_10(in_10));
  Timer timer_1 (.in_1(out_20), .in_2(out_24), .in_3(in_8), .in_4(in_7), .Ready(Stop0));
  or or_2 (out_21, CSI, out_20, CSD);
  D_Flip_Flop #(.trigger("falling")) d_ff_2 (.clk(in_8), .D(Stop0), .Q(out_24));  // open: Qn, preset, en, reset
  Read_Ram read_ram_2 (
    .in_1(in_1), .in_2(in_2), .in_3(in_3), .in_4(in_4), .in_6(in_6), .in_7(in_8), .in_8(in_9), .in_9(in_12),
    .out_11(DO0), .out_12(DO1), .out_13(DO2), .out_14(DO3), .out_15(CSD), .out_16(out_23), .in_5(in_5[19:4]),
    .in_10(in_10));
  Multiplexer #(.width(32)) multiplexer_1 (.in0(inout_1_output), .in1(IO3), .out(out_17), .sel(in_13));  // open: en
  Demultiplexer #(.select(2)) demultiplexer_1 (
    .out0(out_19[0]), .out1(out_19[1]), .out2(out_19[2]), .out3(out_19[3]), .in(1'b1), .sel(in_5[3:2]));  // open: en
  InOut inout_1 (.in_1(DO3), .Output(inout_1_output));
  Multiplexer #(.width(32)) multiplexer_2 (.in0(inout_2_output), .in1(IO0), .out(out_14), .sel(in_13));  // open: en
  Multiplexer #(.width(32)) multiplexer_3 (.in0(inout_3_output), .in1(IO1), .out(out_15), .sel(in_13));  // open: en
  Multiplexer #(.width(32)) multiplexer_4 (.in0(inout_4_output), .in1(IO2), .out(out_16), .sel(in_13));  // open: en
  InOut inout_2 (.in_1(DO0), .Output(inout_2_output));
  InOut inout_3 (.in_1(DO1), .Output(inout_3_output));
  InOut inout_4 (.in_1(DO2), .Output(inout_4_output));

  assign out_18 = in_5[19:4];

  // Other names for the same wires on the sheet: Bank0[31:0] = in_1; Bank1[31:0] = in_2; Bank2[31:0] = in_3;
  //   Bank3[31:0] = in_4; BankOut0[31:0] = out_14; BankOut1[31:0] = out_15; BankOut2[31:0] = out_16;
  //   BankOut3[31:0] = out_17; Clk = in_8; CS = out_21; DPAddress[31:0] = in_5; ADDR[15:0] = in_5[19:4];
  //   getData = in_12; getInst = in_11; isInst = in_13; MASK[3:0] = out_19; ReadTime[3:0] = in_6; ReadyData = out_23;
  //   ReadyInst = out_22; ReadyWrite = out_24; Reset = in_9; RW = out_20; Write = in_10; WriteTime[3:0] = in_7
endmodule

module Read_Ram (
  input  [31:0] in_1,
  input  [31:0] in_2,
  input  [31:0] in_3,
  input  [31:0] in_4,
  input  [15:0] in_5,
  input  [3:0] in_6,
  input  in_7,
  input  in_8,
  input  in_9,
  input  in_10,
  output [31:0] out_11,
  output [31:0] out_12,
  output [31:0] out_13,
  output [31:0] out_14,
  output out_15,
  output out_16
);

  wire a, and_1_out, and_4_out, comparator_1_eq, Cont, d_ff_5_q, getRead, multiplexer_1_out, not_1_out,
       or_1_out, ReadyRead, ResetMem, RM, Stop, x;
  wire [15:0] ADDRMem;

  or or_1 (or_1_out, getRead, Stop);
  D_Flip_Flop #(.trigger("falling")) d_ff_1 (.clk(in_7), .D(getRead), .Q(a), .en(or_1_out));  // open: Qn, preset, reset
  Register #(.width(32)) register_1 (.D(in_1), .en(x), .Q(out_11), .clk(in_7), .clr(in_8));
  Register #(.width(32)) register_2 (.D(in_2), .en(x), .Q(out_12), .clk(in_7), .clr(in_8));
  Timer timer_1 (.in_1(a), .in_2(ReadyRead), .in_3(in_7), .in_4(in_6), .Ready(Stop));
  Register #(.width(32)) register_3 (.D(in_4), .en(x), .Q(out_14), .clk(in_7), .clr(in_8));
  Register #(.width(32)) register_4 (.D(in_3), .en(x), .Q(out_13), .clk(in_7), .clr(in_8));
  D_Flip_Flop #(.trigger("falling")) d_ff_2 (.clk(in_7), .D(Stop), .Q(x), .reset(ReadyRead));  // open: Qn, preset, en
  D_Flip_Flop #(.trigger("falling")) d_ff_3 (.clk(in_7), .D(x), .Q(ReadyRead));  // open: Qn, preset, en, reset
  or or_2 (RM, and_1_out, in_8);
  and and_1 (and_1_out, in_10, Cont);
  or or_3 (out_15, x, a);
  Comparator_part #(.width(16)) comparator_1 (.a(in_5), .b(ADDRMem), .eq(comparator_1_eq));  // open: gt, lt
  or or_4 (out_16, d_ff_5_q, ReadyRead);
  Multiplexer multiplexer_1 (.in0(ResetMem), .in1(RM), .out(multiplexer_1_out), .sel(RM));  // open: en
  Register #(.width(16)) register_5 (.D(in_5), .en(x), .Q(ADDRMem), .clk(in_7), .clr(in_8));
  and and_2 (Cont, ~ResetMem, comparator_1_eq);  // AND_Gate
  D_Flip_Flop #(.trigger("falling")) d_ff_4 (
    .clk(in_7), .D(multiplexer_1_out), .Q(ResetMem), .reset(ReadyRead));  // open: Qn, preset, en
  and and_3 (getRead, in_9, not_1_out);
  not not_1 (not_1_out, Cont);
  and and_4 (and_4_out, in_9, Cont);
  D_Flip_Flop #(.trigger("falling")) d_ff_5 (
    .clk(in_7), .D(and_4_out), .Q(d_ff_5_q), .reset(in_8));  // open: Qn, preset, en

  // Other names for the same wires on the sheet: ADDR[15:0] = in_5; Bank0[31:0] = in_1; Bank1[31:0] = in_2;
  //   Bank2[31:0] = in_3; Bank3[31:0] = in_4; BankOut0[31:0] = out_11; BankOut1[31:0] = out_12;
  //   BankOut2[31:0] = out_13; BankOut3[31:0] = out_14; Clk = in_7; CS = out_15; get = in_9; ReadTime[3:0] = in_6;
  //   Ready = out_16; Reset = in_8; Write = in_10
endmodule

// BC
module Branch_Control (
  input  [25:0] in_1,
  input  [31:0] in_2,
  input  [31:0] in_3,
  input  [31:0] in_4,
  input  [15:0] in_5,
  input  in_6,
  input  in_7,
  input  in_8,
  input  in_9,
  input  in_10,
  input  in_11,
  input  in_12,
  output [31:0] OUT
);

  wire and_1_out, and_2_out, and_3_out, and_4_out, and_5_out, comparator_1_eq, or_2_out, RS_0, RS__0, RS__RT;
  wire [1:0] or_3_out;
  wire [13:0] bit_extender_1_out;
  wire [31:0] PC_4, PC_4_Const;

  Comparator_part #(.width(32)) comparator_1 (.a(in_2), .b({32{1'b0}}), .eq(comparator_1_eq), .lt(RS_0));  // open: gt
  Comparator_part #(.width(32)) comparator_2 (.a(in_2), .b(in_3), .eq(RS__RT));  // open: gt, lt
  and and_1 (and_1_out, in_6, RS__RT);
  and and_2 (and_2_out, ~RS__RT, in_7);  // AND_Gate
  and and_3 (and_3_out, in_8, RS__0);
  and and_4 (and_4_out, ~RS__0, in_9);  // AND_Gate
  and and_5 (and_5_out, in_10, RS_0);
  or or_1 (RS__0, comparator_1_eq, RS_0);
  or or_2 (or_2_out, and_1_out, and_2_out, and_3_out, and_4_out, and_5_out);
  or or_3 (or_3_out[0], or_2_out, in_11);
  or or_4 (or_3_out[1], in_12, in_11);
  Multiplexer #(.select(2), .width(32)) multiplexer_1 (
    .in0(PC_4), .in1(PC_4_Const), .in2({in_4[31:28], in_1, 2'b00}), .in3(in_2), .out(OUT), .sel(or_3_out));  // open: en
  Adder #(.width(32)) adder_1 (.a(in_4), .b(32'h4), .out(PC_4));  // open: cin, cout
  assign bit_extender_1_out = {{13{in_5[15]}}, in_5[15]};  // Bit_Extender bit_extender_1
  Adder #(.width(32)) adder_2 (.a(PC_4), .b({bit_extender_1_out, in_5, 2'b00}), .out(PC_4_Const));  // open: cin, cout

  // Other names for the same wires on the sheet: Const[15:0] = in_5; Beq = in_6; Bgtz = in_9; Blez = in_8;
  //   Bltz = in_10; Bne = in_7; J = in_12; Dest[25:0] = in_1; Jmp[31:2] = {in_4[31:28], in_1}; PC[31:0] = in_4;
  //   Jr = in_11; RS[31:0] = in_2; RT[31:0] = in_3
endmodule

// MA
module Memory_Adderss (
  input  [31:0] in_1,
  input  [31:0] in_2,
  input  [31:0] in_3,
  input  in_4,
  input  in_5,
  input  in_6,
  input  in_7,
  input  in_8,
  output [31:0] OUT
);

  wire [1:0] or_2_out;
  wire [31:0] multiplexer_1_out, subtractor_1_out;

  Subtractor #(.width(32)) subtractor_1 (.a(in_3), .b(32'h4), .out(subtractor_1_out));  // open: bin, bout
  Multiplexer #(.width(32)) multiplexer_1 (
    .in0(in_3), .in1(subtractor_1_out), .out(multiplexer_1_out), .sel(in_7));  // open: en
  Multiplexer #(.select(2), .width(32)) multiplexer_2 (
    .in0(in_1), .in1(in_2), .in2(multiplexer_1_out), .in3(in_1), .out(OUT), .sel(or_2_out));  // open: en
  or or_1 (or_2_out[1], in_6, in_8, in_7);
  or or_2 (or_2_out[0], in_4, in_8, in_5);

  // Other names for the same wires on the sheet: ALU[31:0] = in_2; isPC = in_8; Lw = in_4; PC[31:0] = in_1;
  //   Pop = in_6; Push = in_7; SP[31:0] = in_3; Sw = in_5
endmodule

module PC (
  input  in_1,
  input  in_2,
  input  in_3,
  input  [31:0] in_4,
  output [31:0] out_5
);

  Register #(.width(32)) register_1 (.D(in_4), .en(in_3), .Q(out_5), .clk(in_2), .clr(in_1));
endmodule

// Multip
module Multiplication (
  input  in_1,
  input  [31:0] X,
  input  [31:0] Y,
  output [31:0] OH,
  output [31:0] OL
);

  wire and_1_out, Overflow, Overflow1, shr_2_out_3, shr_4_out_3, SigX, SigY;
  wire [31:0] NA, NAA, NB, NBB, OH1, OH2, OL1, OL2, RH, RH1, RL, RL1, shl_1_x_2, shl_2_x_2, shr_1_x_2,
       shr_6_x_2, shr_7_x_2, subtractor_1_out, SumX, SumY;

  and and_1 (and_1_out, SigX, SigY);
  SHR shr_1 (.X({32{1'b0}}), .in_2(and_1_out), .X_2(shr_1_x_2));  // open: out_3
  Subtractor #(.width(32)) subtractor_1 (.a(X), .b(shr_1_x_2), .out(subtractor_1_out));  // open: bin, bout
  SHL shl_1 (.X(X), .in_2(1'b0), .out_3(SigX), .X_2(shl_1_x_2));
  SHL shl_2 (.X(Y), .in_2(1'b0), .out_3(SigY), .X_2(shl_2_x_2));
  Multiplexer #(.width(32)) multiplexer_1 (
    .in0({32{1'b0}}), .in1(subtractor_1_out), .out(SumX), .sel(SigY));  // open: en
  Multiplexer #(.width(32)) multiplexer_2 (.in0({32{1'b0}}), .in1(Y), .out(SumY), .sel(SigX));  // open: en
  Multiplier #(.width(32)) multiplier_1 (.a(X), .b(Y), .out(OL1), .cout(OH1));  // open: cin
  Multiplier #(.width(32)) multiplier_2 (.a(shl_1_x_2), .b(shl_2_x_2), .out(OL2), .cout(OH2));  // open: cin
  SHR shr_2 (.X(OL2), .in_2(1'b0), .out_3(shr_2_out_3), .X_2(NA));
  SHR shr_3 (.X(OH2), .in_2(shr_2_out_3), .X_2(NB));  // open: out_3
  SHR shr_4 (.X(NA), .in_2(1'b0), .out_3(shr_4_out_3), .X_2(NAA));
  SHR shr_5 (.X(NB), .in_2(shr_4_out_3), .X_2(NBB));  // open: out_3
  Adder #(.width(32)) adder_1 (.a(NAA), .b(SumX), .out(RL), .cout(Overflow));  // open: cin
  Adder #(.width(32)) adder_2 (.a(RL), .b(SumY), .out(RL1), .cout(Overflow1));  // open: cin
  SHR shr_6 (.X({32{1'b0}}), .in_2(Overflow), .X_2(shr_6_x_2));  // open: out_3
  SHR shr_7 (.X({32{1'b0}}), .in_2(Overflow1), .X_2(shr_7_x_2));  // open: out_3
  Multiplexer #(.width(32)) multiplexer_3 (.in0(RL1), .in1(OL1), .out(OL), .sel(in_1));  // open: en
  Multiplexer #(.width(32)) multiplexer_4 (.in0(RH1), .in1(OH1), .out(OH), .sel(in_1));  // open: en
  Adder #(.width(32)) adder_3 (.a(NBB), .b(shr_6_x_2), .out(RH));  // open: cin, cout
  Adder #(.width(32)) adder_4 (.a(RH), .b(shr_7_x_2), .out(RH1));  // open: cin, cout

  // Other names for the same wires on the sheet: Sign = in_1
endmodule

module Division (
  input  in_1,
  input  [31:0] in_2,
  input  [31:0] in_3,
  output [31:0] DivRem,
  output [31:0] Div
);

  wire shr_1_out_3, shr_2_out_3, SignX, SignY, xor_1_out;
  wire [31:0] adder_1_out, Div_t, multiplexer_4_out, negator_1_out, negator_2_out, negator_3_out, Rem,
       subtractor_1_out, X1, Y1;

  SHR shr_1 (.X(in_2), .in_2(1'b0), .out_3(shr_1_out_3));  // open: X_2
  SHR shr_2 (.X(in_3), .in_2(1'b0), .out_3(shr_2_out_3));  // open: X_2
  Negator #(.width(32)) negator_1 (.in(in_2), .out(negator_1_out));
  Negator #(.width(32)) negator_2 (.in(in_3), .out(negator_2_out));
  and and_1 (SignX, in_1, shr_1_out_3);
  and and_2 (SignY, in_1, shr_2_out_3);
  Multiplexer #(.width(32)) multiplexer_1 (.in0(in_2), .in1(negator_1_out), .out(X1), .sel(SignX));  // open: en
  Multiplexer #(.width(32)) multiplexer_2 (.in0(in_3), .in1(negator_2_out), .out(Y1), .sel(SignY));  // open: en
  Subtractor #(.width(32)) subtractor_1 (.a(Y1), .b(Rem), .out(subtractor_1_out));  // open: bin, bout
  Divider #(.width(32)) divider_1 (.a(X1), .b(Y1), .out(Div_t), .rem(Rem));  // open: upper
  Multiplexer #(.width(32)) multiplexer_3 (.in0(Rem), .in1(subtractor_1_out), .out(DivRem), .sel(SignX));  // open: en
  Adder #(.width(32)) adder_1 (.a(Div_t), .b(32'h1), .out(adder_1_out));  // open: cin, cout
  Multiplexer #(.width(32)) multiplexer_4 (
    .in0(Div_t), .in1(adder_1_out), .out(multiplexer_4_out), .sel(SignX));  // open: en
  Negator #(.width(32)) negator_3 (.in(multiplexer_4_out), .out(negator_3_out));
  Multiplexer #(.width(32)) multiplexer_5 (
    .in0(multiplexer_4_out), .in1(negator_3_out), .out(Div), .sel(xor_1_out));  // open: en
  xor xor_1 (xor_1_out, SignY, SignX);

  // Other names for the same wires on the sheet: OH[31:0] = DivRem; OL[31:0] = Div; Sign = in_1; X[31:0] = in_2;
  //   Y[31:0] = in_3
endmodule

// Comp
module Comparator (
  input  [31:0] in_1,
  input  [31:0] in_2,
  input  in_3,
  output Comp
);

  wire and_1_out, and_2_out, comparator_1_lt, comparator_2_lt;

  Comparator_part #(.width(32)) comparator_1 (.a(in_1), .b(in_2), .lt(comparator_1_lt));  // open: gt, eq
  Comparator_part #(.width(32), .mode("unsigned")) comparator_2 (
    .a(in_1), .b(in_2), .lt(comparator_2_lt));  // open: gt, eq
  and and_1 (and_1_out, comparator_1_lt, in_3);
  and and_2 (and_2_out, ~in_3, comparator_2_lt);  // AND_Gate
  or or_1 (Comp, and_1_out, and_2_out);

  // Other names for the same wires on the sheet: Sign = in_3; X[31:0] = in_1; Y[31:0] = in_2
endmodule

module SHL (
  input  [31:0] X,
  input  in_2,
  output out_3,
  output [31:0] X_2
);


  assign out_3 = X[0];
  assign X_2 = {in_2, X[31:1]};
endmodule

module SHR (
  input  [31:0] X,
  input  in_2,
  output out_3,
  output [31:0] X_2
);


  assign out_3 = X[31];
  assign X_2 = {X[30:0], in_2};
endmodule

// IO
module InOut (
  input  [31:0] in_1,
  output [31:0] Output
);


  assign Output = {in_1[7:0], in_1[15:8], in_1[23:16], in_1[31:24]};
endmodule

module Timer (
  input  in_1,
  input  in_2,
  input  in_3,
  input  [3:0] in_4,
  output Ready
);

  wire [3:0] counter_1_q;

  Counter #(.width(4), .max('hf)) counter_1 (
    .count(in_1), .Q(counter_1_q), .clk(in_3), .clr(in_2));  // open: load, D, carry
  Comparator_part #(.width(4)) comparator_1 (.a(in_4), .b(counter_1_q), .eq(Ready));  // open: gt, lt

  // Other names for the same wires on the sheet: Clk = in_3; Reset = in_2; Start = in_1; Time[3:0] = in_4
endmodule
